// Logisim project Logisim-College Work.circ as structural Verilog: 32 circuits, main circuit Half Adder
// HA
module Half_Adder (
  input  A,
  input  B,
  output Sum,
  output Carry
);

  wire nand_1_out, nand_2_out, nand_3_out, nand_4_out, nand_5_out;

  nand nand_1 (nand_1_out, A, A);
  nand nand_2 (nand_2_out, B, B);
  nand nand_3 (nand_3_out, A, B);
  nand nand_4 (nand_4_out, nand_1_out, B);
  nand nand_5 (nand_5_out, A, nand_2_out);
  nand nand_6 (Carry, nand_3_out, nand_3_out);
  nand nand_7 (Sum, nand_4_out, nand_5_out);

  // Notes on the sheet:
  //   HALF ADDER
endmodule

// FA
module Full_Adder (
  input  A,
  input  B,
  input  C,
  output Sum,
  output Carry
);

  wire nand_1_out, nand_2_out, nand_3_out, nand_4_out, nand_5_out, nand_6_out, nand_7_out, nand_8_out,
       nand_9_out, nand_10_out, nand_11_out, nand_12_out, nand_13_out;

  nand nand_1 (nand_1_out, A, A);
  nand nand_2 (nand_2_out, B, B);
  nand nand_3 (nand_3_out, A, A);
  nand nand_4 (nand_4_out, C, C);
  nand nand_5 (nand_5_out, B, B);
  nand nand_6 (nand_6_out, C, C);
  nand nand_7 (nand_7_out, B, C);
  nand nand_8 (nand_8_out, A, C);
  nand nand_9 (nand_9_out, A, B);
  nand nand_10 (nand_10_out, nand_1_out, nand_2_out, C);
  nand nand_11 (nand_11_out, nand_3_out, B, nand_4_out);
  nand nand_12 (nand_12_out, A, nand_5_out, nand_6_out);
  nand nand_13 (nand_13_out, A, B, C);
  nand nand_14 (Carry, nand_7_out, nand_8_out, nand_9_out);
  nand nand_15 (Sum, nand_10_out, nand_11_out, nand_12_out, nand_13_out);

  // Notes on the sheet:
  //   FULL ADDER
endmodule

module _4bit_parallelAdder (
  input  [3:0] A3A2A1A0,
  input  [3:0] B3B2B1B0,
  input  Cin,
  output [3:0] S3S2S1S0,
  output Cout,
  output Overflow
);

  wire full_adder_2_carry, full_adder_3_carry, full_adder_4_carry;

  Full_Adder full_adder_1 (.A(full_adder_2_carry), .B(A3A2A1A0[3]), .C(B3B2B1B0[3]), .Sum(S3S2S1S0[3]), .Carry(Cout));
  Full_Adder full_adder_2 (
    .A(full_adder_3_carry), .B(A3A2A1A0[2]), .C(B3B2B1B0[2]), .Sum(S3S2S1S0[2]), .Carry(full_adder_2_carry));
  Full_Adder full_adder_3 (
    .A(full_adder_4_carry), .B(A3A2A1A0[1]), .C(B3B2B1B0[1]), .Sum(S3S2S1S0[1]), .Carry(full_adder_3_carry));
  xor xor_1 (Overflow, full_adder_2_carry, Cout);
  Full_Adder full_adder_4 (.A(Cin), .B(A3A2A1A0[0]), .C(B3B2B1B0[0]), .Sum(S3S2S1S0[0]), .Carry(full_adder_4_carry));

  // Notes on the sheet:
  //   4-Bit Adder 
endmodule

module _4bit_paraAdder_subtr (
  input  Cin___control,
  input  [3:0] A3A2A1A0,
  input  [3:0] B3B2B1B0,
  output [3:0] S3S2S1S0,
  output Cout
);

  wire full_adder_1_carry, full_adder_2_carry, full_adder_3_carry, xor_2_out, xor_3_out, xor_4_out, xor_out;

  xor \xor  (xor_out, Cin___control, B3B2B1B0[0]);
  xor xor_2 (xor_2_out, Cin___control, B3B2B1B0[1]);
  xor xor_3 (xor_3_out, Cin___control, B3B2B1B0[2]);
  xor xor_4 (xor_4_out, Cin___control, B3B2B1B0[3]);
  Full_Adder full_adder_1 (
    .A(Cin___control), .B(A3A2A1A0[0]), .C(xor_out), .Sum(S3S2S1S0[0]), .Carry(full_adder_1_carry));
  Full_Adder full_adder_2 (
    .A(full_adder_1_carry), .B(A3A2A1A0[1]), .C(xor_2_out), .Sum(S3S2S1S0[1]), .Carry(full_adder_2_carry));
  Full_Adder full_adder_3 (
    .A(full_adder_2_carry), .B(A3A2A1A0[2]), .C(xor_3_out), .Sum(S3S2S1S0[2]), .Carry(full_adder_3_carry));
  Full_Adder full_adder_4 (.A(full_adder_3_carry), .B(A3A2A1A0[3]), .C(xor_4_out), .Sum(S3S2S1S0[3]), .Carry(Cout));

  // Notes on the sheet:
  //   4-Bit Adder / Substracter
endmodule

// MUX
module _2x1_MUX (
  input  D0,
  input  D,
  input  S0,
  output Output
);

  wire and_1_out, and_2_out, not_1_out;

  not not_1 (not_1_out, S0);
  and and_1 (and_1_out, not_1_out, D0);
  and and_2 (and_2_out, S0, D);
  or or_1 (Output, and_1_out, and_2_out);
endmodule

module _4x1_MUX (
  input  D0,
  input  D1,
  input  D2,
  input  D3,
  input  S0,
  input  S1,
  output Y
);

  wire nand_1_out, nand_2_out, nand_3_out, nand_4_out, nand_5_out, nand_6_out, nand_7_out, nand_8_out;

  nand nand_1 (nand_1_out, S1, S1);
  nand nand_2 (nand_2_out, S0, S0);
  nand nand_3 (nand_3_out, S1, S1);
  nand nand_4 (nand_4_out, S0, S0);
  nand nand_5 (nand_5_out, nand_1_out, nand_2_out, D0);
  nand nand_6 (nand_6_out, nand_3_out, S0, D1);
  nand nand_7 (nand_7_out, S1, nand_4_out, D2);
  nand nand_8 (nand_8_out, S1, S0, D3);
  nand nand_9 (Y, nand_5_out, nand_6_out, nand_7_out, nand_8_out);
endmodule

// AU
module Arithmetic_Unit_AU (
  input  Cin,
  input  A0,
  input  B0,
  input  constant_0_1,
  input  S0,
  input  S1,
  output \output ,
  output Cout
);

  wire n4x1_mux_1_y, not_1_out, not_2_out;

  not not_1 (not_1_out, B0);
  not not_2 (not_2_out, constant_0_1);
  _4x1_MUX u_4x1_mux_1 (.D0(B0), .D1(not_1_out), .D2(constant_0_1), .D3(not_2_out), .S0(S0), .S1(S1), .Y(n4x1_mux_1_y));
  Full_Adder full_adder_1 (.A(Cin), .B(A0), .C(n4x1_mux_1_y), .Sum(\output ), .Carry(Cout));
endmodule

// LU
module Logic_unit_LU (
  input  A,
  input  B,
  input  S0,
  input  S1,
  output Output
);

  wire AND_out, not_1_out, OR_out, XOR_out;

  and AND (AND_out, A, B);
  or OR (OR_out, A, B);
  xor XOR (XOR_out, A, B);
  not not_1 (not_1_out, A);
  _4x1_MUX u_4x1_mux_1 (.D0(AND_out), .D1(OR_out), .D2(XOR_out), .D3(not_1_out), .S0(S0), .S1(S1), .Y(Output));
endmodule

// ALU
module single_stage_ALU (
  input  Cin,
  input  A0,
  input  B0,
  input  constant_0_1,
  input  [1:0] S1_S0,
  input  S2,
  output Y0,
  output Z0
);

  wire arithmetic_unit_au_1_output, logic_unit_lu_1_output;

  Arithmetic_Unit_AU arithmetic_unit_au_1 (
    .Cin(Cin), .A0(A0), .B0(B0), .constant_0_1(constant_0_1), .S0(S1_S0[1]), .S1(S1_S0[0]),
    .\output (arithmetic_unit_au_1_output), .Cout(Z0));
  Logic_unit_LU logic_unit_lu_1 (.A(B0), .B(A0), .S0(S1_S0[1]), .S1(S1_S0[0]), .Output(logic_unit_lu_1_output));
  _2x1_MUX u_2x1_mux_1 (.D0(arithmetic_unit_au_1_output), .D(logic_unit_lu_1_output), .S0(S2), .Output(Y0));
endmodule

module _4_bit_AU (
  input  Cin,
  input  [3:0] A3A2A1A0,
  input  [3:0] B3B2B1B0,
  input  [3:0] Constant,
  input  S0,
  input  S1,
  output [3:0] Y3Y2Y1Y0,
  output Zero_Flag,
  output Parity_flag,
  output Overflow,
  output Cout
);

  wire arithmetic_unit_au_1_cout, arithmetic_unit_au_2_cout, arithmetic_unit_au_3_cout, xnor_1_out,
       xnor_2_out;

  Arithmetic_Unit_AU arithmetic_unit_au_1 (
    .Cin(Cin), .A0(A3A2A1A0[0]), .B0(B3B2B1B0[0]), .constant_0_1(Constant[0]), .S0(S0), .S1(S1),
    .\output (Y3Y2Y1Y0[0]), .Cout(arithmetic_unit_au_1_cout));
  Arithmetic_Unit_AU arithmetic_unit_au_2 (
    .Cin(arithmetic_unit_au_1_cout), .A0(A3A2A1A0[1]), .B0(B3B2B1B0[1]), .constant_0_1(Constant[1]), .S0(S0),
    .S1(S1), .\output (Y3Y2Y1Y0[1]), .Cout(arithmetic_unit_au_2_cout));
  Arithmetic_Unit_AU arithmetic_unit_au_3 (
    .Cin(arithmetic_unit_au_2_cout), .A0(A3A2A1A0[2]), .B0(B3B2B1B0[2]), .constant_0_1(Constant[2]), .S0(S0),
    .S1(S1), .\output (Y3Y2Y1Y0[2]), .Cout(arithmetic_unit_au_3_cout));
  Arithmetic_Unit_AU arithmetic_unit_au_4 (
    .Cin(arithmetic_unit_au_3_cout), .A0(A3A2A1A0[3]), .B0(B3B2B1B0[3]), .constant_0_1(Constant[3]), .S0(S0),
    .S1(S1), .\output (Y3Y2Y1Y0[3]), .Cout(Cout));
  xor xor_1 (Overflow, arithmetic_unit_au_3_cout, Cout);
  nor nor_1 (Zero_Flag, Y3Y2Y1Y0[0], Y3Y2Y1Y0[1], Y3Y2Y1Y0[2], Y3Y2Y1Y0[3]);
  xnor xnor_1 (xnor_1_out, Y3Y2Y1Y0[0], Y3Y2Y1Y0[1]);
  xnor xnor_2 (xnor_2_out, Y3Y2Y1Y0[2], Y3Y2Y1Y0[3]);
  xnor xnor_3 (Parity_flag, xnor_1_out, xnor_2_out);
endmodule

module _4_bit_LU (
  input  [3:0] A3A2A1A0,
  input  [3:0] B3B2B1B0,
  input  S0,
  input  S1,
  output [3:0] Y3Y2Y1Y0
);

  Logic_unit_LU logic_unit_lu_1 (.A(A3A2A1A0[0]), .B(B3B2B1B0[0]), .S0(S0), .S1(S1), .Output(Y3Y2Y1Y0[0]));
  Logic_unit_LU logic_unit_lu_2 (.A(A3A2A1A0[1]), .B(B3B2B1B0[1]), .S0(S0), .S1(S1), .Output(Y3Y2Y1Y0[1]));
  Logic_unit_LU logic_unit_lu_3 (.A(A3A2A1A0[2]), .B(B3B2B1B0[2]), .S0(S0), .S1(S1), .Output(Y3Y2Y1Y0[2]));
  Logic_unit_LU logic_unit_lu_4 (.A(A3A2A1A0[3]), .B(B3B2B1B0[3]), .S0(S0), .S1(S1), .Output(Y3Y2Y1Y0[3]));
endmodule

module _4_bit_ALU (
  input  Cin,
  input  [3:0] A3A2A1A0,
  input  [3:0] B3B2B1B0,
  input  [3:0] Constant,
  input  [1:0] S1S0,
  input  S2,
  output [3:0] Y3Y2Y1Y0,
  output Zero_Flag,
  output Parity_Flag,
  output Overflow,
  output Cout
);

  wire single_stage_alu_1_z0, single_stage_alu_2_z0, single_stage_alu_3_z0, xnor_1_out, xnor_2_out;

  single_stage_ALU single_stage_alu_1 (
    .Cin(Cin), .A0(A3A2A1A0[0]), .B0(B3B2B1B0[0]), .constant_0_1(Constant[0]), .S1_S0(S1S0), .S2(S2),
    .Y0(Y3Y2Y1Y0[0]), .Z0(single_stage_alu_1_z0));
  single_stage_ALU single_stage_alu_2 (
    .Cin(single_stage_alu_1_z0), .A0(A3A2A1A0[1]), .B0(B3B2B1B0[1]), .constant_0_1(Constant[1]),
    .S1_S0(S1S0), .S2(S2), .Y0(Y3Y2Y1Y0[1]), .Z0(single_stage_alu_2_z0));
  single_stage_ALU single_stage_alu_3 (
    .Cin(single_stage_alu_2_z0), .A0(A3A2A1A0[2]), .B0(B3B2B1B0[2]), .constant_0_1(Constant[2]),
    .S1_S0(S1S0), .S2(S2), .Y0(Y3Y2Y1Y0[2]), .Z0(single_stage_alu_3_z0));
  single_stage_ALU single_stage_alu_4 (
    .Cin(single_stage_alu_3_z0), .A0(A3A2A1A0[3]), .B0(B3B2B1B0[3]), .constant_0_1(Constant[3]),
    .S1_S0(S1S0), .S2(S2), .Y0(Y3Y2Y1Y0[3]), .Z0(Cout));
  xor xor_1 (Overflow, single_stage_alu_3_z0, Cout);
  nor nor_1 (Zero_Flag, Y3Y2Y1Y0[0], Y3Y2Y1Y0[1], Y3Y2Y1Y0[2], Y3Y2Y1Y0[3]);
  xnor xnor_1 (xnor_1_out, Y3Y2Y1Y0[0], Y3Y2Y1Y0[1]);
  xnor xnor_2 (xnor_2_out, Y3Y2Y1Y0[2], Y3Y2Y1Y0[3]);
  xnor xnor_3 (Parity_Flag, xnor_1_out, xnor_2_out);
endmodule

module _2to4_decoder (
  input  A,
  input  B,
  output Y0,
  output Y1,
  output Y2,
  output Y3
);

  wire nand_1_out, nand_2_out, nand_3_out, nand_4_out, nand_5_out, nand_6_out, nand_7_out, nand_8_out;

  nand nand_1 (nand_1_out, A, A);
  nand nand_2 (nand_2_out, B, B);
  nand nand_3 (nand_3_out, A, A);
  nand nand_4 (nand_4_out, B, B);
  nand nand_5 (nand_5_out, A, B);
  nand nand_6 (nand_6_out, nand_1_out, nand_2_out);
  nand nand_7 (nand_7_out, nand_3_out, B);
  nand nand_8 (nand_8_out, A, nand_4_out);
  nand nand_9 (Y3, nand_5_out, nand_5_out);
  nand nand_10 (Y0, nand_6_out, nand_6_out);
  nand nand_11 (Y1, nand_7_out, nand_7_out);
  nand nand_12 (Y2, nand_8_out, nand_8_out);
endmodule

module Register_File_Write_Read___ALU (
  input  [1:0] RegRead1,
  input  Write_Enable,
  input  [1:0] Write_Select,
  input  [3:0] Data_Input,
  input  [1:0] RegRead2,
  input  Cin,
  input  [3:0] constant,
  input  [1:0] S1_S0,
  input  S2,
  output [3:0] ReadPort1,
  output [3:0] ReadPort2,
  output [3:0] Y3Y2Y1Y0,
  output Zero_Flag,
  output ParityFlag,
  output OverFlow_Flag,
  output Cout
);

  wire and_1_out, and_2_out, and_3_out, and_4_out, Cloc_out, decoder_y0, decoder_y1, decoder_y2, decoder_y3;
  wire [3:0] register_2_q, register_3_q, register_4_q, Register_q;

  Clock Cloc (.out(Cloc_out));
  _2to4_decoder decoder (
    .A(Write_Select[0]), .B(Write_Select[1]), .Y0(decoder_y0), .Y1(decoder_y1), .Y2(decoder_y2),
    .Y3(decoder_y3));
  and and_1 (and_1_out, decoder_y0, Write_Enable);
  and and_2 (and_2_out, Write_Enable, decoder_y1);
  and and_3 (and_3_out, Write_Enable, decoder_y2);
  and and_4 (and_4_out, Write_Enable, decoder_y3);
  Register #(.width(4)) Register (.D(Data_Input), .en(and_1_out), .Q(Register_q), .clk(Cloc_out));  // open: clr
  Register #(.width(4)) register_2 (.D(Data_Input), .en(and_2_out), .Q(register_2_q), .clk(Cloc_out));  // open: clr
  Register #(.width(4)) register_3 (.D(Data_Input), .en(and_3_out), .Q(register_3_q), .clk(Cloc_out));  // open: clr
  Register #(.width(4)) register_4 (.D(Data_Input), .en(and_4_out), .Q(register_4_q), .clk(Cloc_out));  // open: clr
  _4_bit_ALU u_4_bit_alu_1 (
    .Cin(Cin), .A3A2A1A0(ReadPort1), .B3B2B1B0(ReadPort2), .Constant(constant), .S1S0(S1_S0), .S2(S2),
    .Y3Y2Y1Y0(Y3Y2Y1Y0), .Zero_Flag(Zero_Flag), .Parity_Flag(ParityFlag), .Overflow(OverFlow_Flag),
    .Cout(Cout));
  Multibit_MUX Multibit_MUX (
    .A(Register_q), .B(register_2_q), .C(register_3_q), .D(register_4_q), .S0(RegRead1[0]), .S1(RegRead1[1]),
    .out_7(ReadPort1));
  Multibit_MUX Multibit_MUX_2 (
    .A(Register_q), .B(register_2_q), .C(register_3_q), .D(register_4_q), .S0(RegRead2[0]), .S1(RegRead2[1]),
    .out_7(ReadPort2));

  // Notes on the sheet:
  //   Read Write Register File
endmodule

module Multibit_MUX (
  input  [3:0] A,
  input  [3:0] B,
  input  [3:0] C,
  input  [3:0] D,
  input  S0,
  input  S1,
  output [3:0] out_7
);

  _4x1_MUX u_4x1_mux_1 (.D0(A[0]), .D1(B[0]), .D2(C[0]), .D3(D[0]), .S0(S0), .S1(S1), .Y(out_7[0]));
  _4x1_MUX u_4x1_mux_2 (.D0(A[1]), .D1(B[1]), .D2(C[1]), .D3(D[1]), .S0(S0), .S1(S1), .Y(out_7[1]));
  _4x1_MUX u_4x1_mux_3 (.D0(A[2]), .D1(B[2]), .D2(C[2]), .D3(D[2]), .S0(S0), .S1(S1), .Y(out_7[2]));
  _4x1_MUX u_4x1_mux_4 (.D0(A[3]), .D1(B[3]), .D2(C[3]), .D3(D[3]), .S0(S0), .S1(S1), .Y(out_7[3]));
endmodule

module Array_Multiplier (
  input  [3:0] Multiplicand,
  input  [3:0] Multiplier,
  output [7:0] out_3
);

  wire and_1_out, and_2_out, and_3_out, and_4_out, and_5_out, and_6_out, and_7_out, and_8_out, and_9_out,
       and_10_out, and_11_out, and_12_out, and_13_out, and_14_out, and_16_out, full_adder_2_carry,
       full_adder_2_sum, full_adder_3_carry, full_adder_4_carry, full_adder_5_carry, full_adder_5_sum,
       full_adder_6_carry, full_adder_6_sum, full_adder_7_carry, full_adder_7_sum, full_adder_8_carry,
       full_adder_8_sum, half_adder_1_carry, half_adder_1_sum, half_adder_2_carry, half_adder_3_carry,
       half_adder_4_carry;

  and and_1 (and_1_out, Multiplicand[2], Multiplier[3]);
  and and_2 (and_2_out, Multiplicand[3], Multiplier[3]);
  Full_Adder full_adder_1 (
    .A(full_adder_3_carry), .B(and_2_out), .C(full_adder_2_carry), .Sum(out_3[6]), .Carry(out_3[7]));
  and and_3 (and_3_out, Multiplicand[3], Multiplier[2]);
  Full_Adder full_adder_2 (
    .A(full_adder_5_carry), .B(and_3_out), .C(half_adder_1_carry), .Sum(full_adder_2_sum),
    .Carry(full_adder_2_carry));
  and and_4 (and_4_out, Multiplicand[1], Multiplier[3]);
  Full_Adder full_adder_3 (
    .A(full_adder_4_carry), .B(and_1_out), .C(full_adder_2_sum), .Sum(out_3[5]), .Carry(full_adder_3_carry));
  Full_Adder full_adder_4 (
    .A(half_adder_2_carry), .B(and_4_out), .C(full_adder_5_sum), .Sum(out_3[4]), .Carry(full_adder_4_carry));
  and and_5 (and_5_out, Multiplicand[3], Multiplier[0]);
  and and_6 (and_6_out, Multiplicand[3], Multiplier[1]);
  Half_Adder half_adder_1 (.A(and_6_out), .B(full_adder_6_carry), .Sum(half_adder_1_sum), .Carry(half_adder_1_carry));
  and and_7 (and_7_out, Multiplicand[2], Multiplier[2]);
  and and_8 (and_8_out, Multiplicand[1], Multiplier[2]);
  Full_Adder full_adder_5 (
    .A(full_adder_7_carry), .B(and_7_out), .C(half_adder_1_sum), .Sum(full_adder_5_sum),
    .Carry(full_adder_5_carry));
  and and_9 (and_9_out, Multiplicand[0], Multiplier[3]);
  Half_Adder half_adder_2 (.A(full_adder_7_sum), .B(and_9_out), .Sum(out_3[3]), .Carry(half_adder_2_carry));
  and and_10 (and_10_out, Multiplicand[2], Multiplier[0]);
  and and_11 (and_11_out, Multiplicand[2], Multiplier[1]);
  Full_Adder full_adder_6 (
    .A(full_adder_8_carry), .B(and_11_out), .C(and_5_out), .Sum(full_adder_6_sum), .Carry(full_adder_6_carry));
  and and_12 (and_12_out, Multiplicand[0], Multiplier[2]);
  Half_Adder half_adder_3 (.A(full_adder_8_sum), .B(and_12_out), .Sum(out_3[2]), .Carry(half_adder_3_carry));
  Full_Adder full_adder_7 (
    .A(half_adder_3_carry), .B(and_8_out), .C(full_adder_6_sum), .Sum(full_adder_7_sum),
    .Carry(full_adder_7_carry));
  and and_13 (and_13_out, Multiplicand[1], Multiplier[0]);
  and and_14 (and_14_out, Multiplicand[1], Multiplier[1]);
  Full_Adder full_adder_8 (
    .A(half_adder_4_carry), .B(and_14_out), .C(and_10_out), .Sum(full_adder_8_sum), .Carry(full_adder_8_carry));
  and and_15 (out_3[0], Multiplicand[0], Multiplier[0]);
  and and_16 (and_16_out, Multiplicand[0], Multiplier[1]);
  Half_Adder half_adder_4 (.A(and_16_out), .B(and_13_out), .Sum(out_3[1]), .Carry(half_adder_4_carry));
endmodule

module Sequence_Multiplier (
  input  EN,
  input  EN_2,
  input  CLR,
  input  CLR_2,
  input  data,
  input  S,
  input  [3:0] Bunch_of_zeros,
  input  [3:0] Multiplicand,
  input  Cin,
  output [3:0] \output ,
  output [3:0] Y,
  output Cout,
  output [3:0] Y_2
);

  wire clock_1_out, d_ff_5_q, d_ff_6_q, d_ff_7_q, d_ff_8_q, n2x1_mux_1_output, n2x1_mux_2_output,
       n2x1_mux_3_output, n2x1_mux_4_output;
  wire [3:0] undriven;

  Clock clock_1 (.out(clock_1_out));
  _2x1_MUX u_2x1_mux_1 (.D0(data), .D(Y_2[3]), .S0(S), .Output(n2x1_mux_1_output));
  D_Flip_Flop d_ff_1 (
    .clk(clock_1_out), .D(n2x1_mux_1_output), .Q(\output [3]), .en(EN_2), .reset(CLR_2));  // open: Qn, preset
  _2x1_MUX u_2x1_mux_2 (.D0(\output [3]), .D(Y_2[2]), .S0(S), .Output(n2x1_mux_2_output));
  D_Flip_Flop d_ff_2 (
    .clk(clock_1_out), .D(n2x1_mux_2_output), .Q(\output [2]), .en(EN_2), .reset(CLR_2));  // open: Qn, preset
  _2x1_MUX u_2x1_mux_3 (.D0(\output [2]), .D(Y_2[1]), .S0(S), .Output(n2x1_mux_3_output));
  _4bit_parallelAdder u_4bit_paralleladder_1 (
    .A3A2A1A0(\output ), .B3B2B1B0(Y), .Cin(Cin), .S3S2S1S0(Y_2), .Cout(Cout));  // open: Overflow
  D_Flip_Flop d_ff_3 (
    .clk(clock_1_out), .D(n2x1_mux_3_output), .Q(\output [1]), .en(EN_2), .reset(CLR_2));  // open: Qn, preset
  _2x1_MUX u_2x1_mux_4 (.D0(\output [1]), .D(Y_2[0]), .S0(S), .Output(n2x1_mux_4_output));
  D_Flip_Flop d_ff_4 (
    .clk(clock_1_out), .D(n2x1_mux_4_output), .Q(\output [0]), .en(EN_2), .reset(CLR_2));  // open: Qn, preset
  D_Flip_Flop d_ff_5 (.clk(clock_1_out), .D(\output [0]), .Q(d_ff_5_q), .en(EN), .reset(CLR));  // open: Qn, preset
  D_Flip_Flop d_ff_6 (.clk(clock_1_out), .D(d_ff_5_q), .Q(d_ff_6_q), .en(EN), .reset(CLR));  // open: Qn, preset
  D_Flip_Flop d_ff_7 (.clk(clock_1_out), .D(d_ff_6_q), .Q(d_ff_7_q), .en(EN), .reset(CLR));  // open: Qn, preset
  D_Flip_Flop d_ff_8 (.clk(clock_1_out), .D(d_ff_7_q), .Q(d_ff_8_q), .en(EN), .reset(CLR));  // open: Qn, preset
  _2_1_Multibit u_2_1_multibit_1 (.A(Bunch_of_zeros), .B(undriven), .S0(d_ff_8_q), .Y(Y));
endmodule

module _2_1_Multibit (
  input  [3:0] A,
  input  [3:0] B,
  input  S0,
  output [3:0] Y
);

  _2x1_MUX u_2x1_mux_1 (.D0(A[0]), .D(B[0]), .S0(S0), .Output(Y[0]));
  _2x1_MUX u_2x1_mux_2 (.D0(A[1]), .D(B[1]), .S0(S0), .Output(Y[1]));
  _2x1_MUX u_2x1_mux_3 (.D0(A[2]), .D(B[2]), .S0(S0), .Output(Y[2]));
  _2x1_MUX u_2x1_mux_4 (.D0(A[3]), .D(B[3]), .S0(S0), .Output(Y[3]));
endmodule

module ALU_control (
  input  Alu_c1,
  input  Alu_c2,
  input  F2,
  input  F1,
  input  F0,
  output s2,
  output s1,
  output s0,
  output Cin
);

  wire and_2_out, and_3_out, and_4_out, and_5_out, and_6_out, not_1_out;

  not not_1 (not_1_out, F0);
  and and_1 (s1, Alu_c1, F2, F1);
  and and_2 (and_2_out, Alu_c1, F0);
  and and_3 (and_3_out, Alu_c1, F1);
  and and_4 (and_4_out, Alu_c1, F1);
  and and_5 (and_5_out, Alu_c1, F2, not_1_out);
  and and_6 (and_6_out, Alu_c1, F2, F1);
  or or_1 (s0, Alu_c2, and_2_out, and_3_out);
  or or_2 (Cin, Alu_c2, and_4_out);
  or or_3 (s2, and_5_out, and_6_out);
endmodule

module _4bit_Processor (
  input  Write_Enable,
  input  PC,
  input  [3:0] Start,
  input  B,
  input  [3:0] constant,
  input  [1:0] S1_S0,
  input  Mem_Write,
  input  Mem_Read,
  input  [3:0] in_9,
  input  S2,
  input  [7:0] B_2,
  input  in_12,
  input  [2:0] B_3,
  output [3:0] ReadPort1,
  output [7:0] Instruction,
  output [3:0] Y3Y2Y1Y0,
  output Zero_Flag,
  output ParityFlag,
  output OverFlow_Flag,
  output Cout,
  output [3:0] ReadPort2
);

  wire _2to4_decoder_y2, _2to4_decoder_y3, alu_control_1_cin, and_1_out, and_2_out, and_3_out, and_4_out,
       Cloc_out, clock_1_out, decoder_y0, decoder_y1, decoder_y2, decoder_y3;
  wire [3:0] _2_to_1_mux_y, counter_q, register_2_q, register_3_q, register_4_q, Register_q;

  Clock clock_1 (.out(clock_1_out));
  Counter #(.width(4), .max('hf)) counter (
    .load(PC), .D(Start), .count(B), .Q(counter_q), .clk(clock_1_out));  // open: carry, clr
  _2to4_decoder _2to4_decoder (
    .A(Instruction[7]), .B(Instruction[6]), .Y2(_2to4_decoder_y2), .Y3(_2to4_decoder_y3));  // open: Y0, Y1
  RAM #(.addrWidth(4), .bus("separate")) ram_1 (
    .addr(counter_q), .din(B_2), .data(Instruction), .str(Mem_Write), .clk(clock_1_out), .ld(Mem_Read));  // open: sel, clr
  _2_1_Multibit _2_to_1_mux (.A(in_9), .S0(in_12), .Y(_2_to_1_mux_y));  // open: B
  ALU_control alu_control_1 (
    .Alu_c1(_2to4_decoder_y2), .Alu_c2(_2to4_decoder_y3), .F2(B_3[0]), .F1(B_3[1]), .F0(B_3[2]),
    .Cin(alu_control_1_cin));  // open: s2, s1, s0
  _2to4_decoder decoder (
    .A(Instruction[5]), .B(Instruction[4]), .Y0(decoder_y0), .Y1(decoder_y1), .Y2(decoder_y2), .Y3(decoder_y3));
  and and_1 (and_1_out, decoder_y0, Write_Enable);
  and and_2 (and_2_out, Write_Enable, decoder_y1);
  and and_3 (and_3_out, Write_Enable, decoder_y2);
  and and_4 (and_4_out, Write_Enable, decoder_y3);
  Clock Cloc (.out(Cloc_out));
  Register #(.width(4)) Register (.D(_2_to_1_mux_y), .en(and_1_out), .Q(Register_q), .clk(Cloc_out));  // open: clr
  Register #(.width(4)) register_2 (.D(_2_to_1_mux_y), .en(and_2_out), .Q(register_2_q), .clk(Cloc_out));  // open: clr
  Register #(.width(4)) register_3 (.D(_2_to_1_mux_y), .en(and_3_out), .Q(register_3_q), .clk(Cloc_out));  // open: clr
  Register #(.width(4)) register_4 (.D(_2_to_1_mux_y), .en(and_4_out), .Q(register_4_q), .clk(Cloc_out));  // open: clr
  Multibit_MUX Multibit_MUX (
    .A(Register_q), .B(register_2_q), .C(register_3_q), .D(register_4_q), .S0(Instruction[1]),
    .S1(Instruction[0]), .out_7(ReadPort1));
  Multibit_MUX Multibit_MUX_2 (
    .A(Register_q), .B(register_2_q), .C(register_3_q), .D(register_4_q), .S0(Instruction[3]),
    .S1(Instruction[2]), .out_7(ReadPort2));
  _4_bit_ALU u_4_bit_alu_1 (
    .Cin(alu_control_1_cin), .A3A2A1A0(ReadPort1), .B3B2B1B0(ReadPort2), .Constant(constant), .S1S0(S1_S0),
    .S2(S2), .Y3Y2Y1Y0(Y3Y2Y1Y0), .Zero_Flag(Zero_Flag), .Parity_Flag(ParityFlag), .Overflow(OverFlow_Flag),
    .Cout(Cout));

  // Notes on the sheet:
  //   counter
  //   RAM
endmodule

module Logical_Shifter (
  input  SERIAL_I_P_IR,
  input  select,
  input  [3:0] A0A1A2A3,
  input  SERIAL_I_P_IL,
  output [3:0] H0H1H2H3
);
endmodule

module _16bit_adder (
  input  [15:0] B,
  input  [15:0] A,
  input  in_3,
  output [15:0] out_4,
  output out_5,
  output out_6
);

  wire clock_1_out, n4bit_paralleladder_2_cout, n4bit_paralleladder_3_cout, n4bit_paralleladder_4_cout;

  _4bit_parallelAdder u_4bit_paralleladder_1 (
    .A3A2A1A0(A[15:12]), .B3B2B1B0(B[15:12]), .Cin(n4bit_paralleladder_2_cout), .S3S2S1S0(out_4[15:12]),
    .Cout(out_5), .Overflow(out_6));
  _4bit_parallelAdder u_4bit_paralleladder_2 (
    .A3A2A1A0(A[11:8]), .B3B2B1B0(B[11:8]), .Cin(n4bit_paralleladder_3_cout), .S3S2S1S0(out_4[11:8]),
    .Cout(n4bit_paralleladder_2_cout));  // open: Overflow
  _4bit_parallelAdder u_4bit_paralleladder_3 (
    .A3A2A1A0(A[7:4]), .B3B2B1B0(B[7:4]), .Cin(n4bit_paralleladder_4_cout), .S3S2S1S0(out_4[7:4]),
    .Cout(n4bit_paralleladder_3_cout));  // open: Overflow
  _4bit_parallelAdder u_4bit_paralleladder_4 (
    .A3A2A1A0(A[3:0]), .B3B2B1B0(B[3:0]), .Cin(in_3), .S3S2S1S0(out_4[3:0]), .Cout(n4bit_paralleladder_4_cout));  // open: Overflow
  Clock clock_1 (.out(clock_1_out));
  Register #(.width(16)) register_1 (.D(out_4), .clk(clock_1_out));  // open: en, Q, clr
endmodule

module _8bit_adder_sub (
  input  Cin,
  input  [7:0] A,
  input  [7:0] B,
  output [7:0] out_4,
  output out_5,
  output Cout
);

  wire full_adder_1_carry, full_adder_2_carry, full_adder_3_carry, full_adder_4_carry, full_adder_5_carry,
       full_adder_6_carry, full_adder_7_carry, xor_1_out, xor_2_out, xor_3_out, xor_4_out, xor_5_out,
       xor_6_out, xor_7_out, xor_8_out;

  xor xor_1 (xor_1_out, B[0], Cin);
  xor xor_2 (xor_2_out, B[1], Cin);
  xor xor_3 (xor_3_out, B[2], Cin);
  xor xor_4 (xor_4_out, B[3], Cin);
  xor xor_5 (xor_5_out, B[4], Cin);
  xor xor_6 (xor_6_out, B[5], Cin);
  xor xor_7 (xor_7_out, B[6], Cin);
  xor xor_8 (xor_8_out, B[7], Cin);
  Full_Adder full_adder_1 (.A(Cin), .B(A[0]), .C(xor_1_out), .Sum(out_4[0]), .Carry(full_adder_1_carry));
  Full_Adder full_adder_2 (.A(full_adder_1_carry), .B(A[1]), .C(xor_2_out), .Sum(out_4[1]), .Carry(full_adder_2_carry));
  Full_Adder full_adder_3 (.A(full_adder_2_carry), .B(A[2]), .C(xor_3_out), .Sum(out_4[2]), .Carry(full_adder_3_carry));
  Full_Adder full_adder_4 (.A(full_adder_3_carry), .B(A[3]), .C(xor_4_out), .Sum(out_4[3]), .Carry(full_adder_4_carry));
  Full_Adder full_adder_5 (.A(full_adder_4_carry), .B(A[4]), .C(xor_5_out), .Sum(out_4[4]), .Carry(full_adder_5_carry));
  Full_Adder full_adder_6 (.A(full_adder_5_carry), .B(A[5]), .C(xor_6_out), .Sum(out_4[5]), .Carry(full_adder_6_carry));
  Full_Adder full_adder_7 (.A(full_adder_6_carry), .B(A[6]), .C(xor_7_out), .Sum(out_4[6]), .Carry(full_adder_7_carry));
  Full_Adder full_adder_8 (.A(full_adder_7_carry), .B(A[7]), .C(xor_8_out), .Sum(out_4[7]), .Carry(Cout));
  xor xor_9 (out_5, full_adder_7_carry, Cout);
endmodule

module _8bit_LU (
  input  [7:0] A,
  input  [7:0] B,
  input  S0,
  input  S1,
  output [7:0] out_5
);

  _4_bit_LU u_4_bit_lu_1 (.A3A2A1A0(A[3:0]), .B3B2B1B0(B[3:0]), .S0(S0), .S1(S1), .Y3Y2Y1Y0(out_5[3:0]));
  _4_bit_LU u_4_bit_lu_2 (.A3A2A1A0(A[7:4]), .B3B2B1B0(B[7:4]), .S0(S0), .S1(S1), .Y3Y2Y1Y0(out_5[7:4]));
endmodule

module _8___8bit_register_file (
  input  Write_Enable,
  input  [2:0] Write_Select,
  input  [7:0] Data,
  input  [2:0] S2S1S0,
  input  [2:0] S2S1S0_2,
  output [7:0] out_6,
  output [7:0] out_7
);

  wire and_1_out, and_2_out, and_3_out, and_4_out, and_5_out, and_6_out, and_7_out, and_8_out, Clk_out,
       n3_to_8_decoder_1_d0, n3_to_8_decoder_1_d1, n3_to_8_decoder_1_d2, n3_to_8_decoder_1_d3,
       n3_to_8_decoder_1_d4, n3_to_8_decoder_1_d5, n3_to_8_decoder_1_d6, n3_to_8_decoder_1_d7;
  wire [7:0] register_1_q, register_2_q, register_3_q, register_4_q, register_5_q, register_6_q,
       register_7_q, register_8_q;

  _3_to_8_decoder u_3_to_8_decoder_1 (
    .A(Write_Select[0]), .B(Write_Select[1]), .C(Write_Select[2]), .D0(n3_to_8_decoder_1_d0),
    .D1(n3_to_8_decoder_1_d1), .D2(n3_to_8_decoder_1_d2), .D3(n3_to_8_decoder_1_d3),
    .D4(n3_to_8_decoder_1_d4), .D5(n3_to_8_decoder_1_d5), .D6(n3_to_8_decoder_1_d6), .D7(n3_to_8_decoder_1_d7));
  Clock Clk (.out(Clk_out));
  and and_1 (and_1_out, n3_to_8_decoder_1_d0, Write_Enable);
  and and_2 (and_2_out, n3_to_8_decoder_1_d1, Write_Enable);
  and and_3 (and_3_out, n3_to_8_decoder_1_d2, Write_Enable);
  and and_4 (and_4_out, n3_to_8_decoder_1_d3, Write_Enable);
  and and_5 (and_5_out, n3_to_8_decoder_1_d4, Write_Enable);
  and and_6 (and_6_out, n3_to_8_decoder_1_d5, Write_Enable);
  and and_7 (and_7_out, n3_to_8_decoder_1_d6, Write_Enable);
  and and_8 (and_8_out, n3_to_8_decoder_1_d7, Write_Enable);
  Register register_1 (.D(Data), .en(and_1_out), .Q(register_1_q), .clk(Clk_out));  // open: clr
  Register register_2 (.D(Data), .en(and_2_out), .Q(register_2_q), .clk(Clk_out));  // open: clr
  Register register_3 (.D(Data), .en(and_3_out), .Q(register_3_q), .clk(Clk_out));  // open: clr
  Register register_4 (.D(Data), .en(and_4_out), .Q(register_4_q), .clk(Clk_out));  // open: clr
  Register register_5 (.D(Data), .en(and_5_out), .Q(register_5_q), .clk(Clk_out));  // open: clr
  Register register_6 (.D(Data), .en(and_6_out), .Q(register_6_q), .clk(Clk_out));  // open: clr
  Register register_7 (.D(Data), .en(and_7_out), .Q(register_7_q), .clk(Clk_out));  // open: clr
  Register register_8 (.D(Data), .en(and_8_out), .Q(register_8_q), .clk(Clk_out));  // open: clr
  Multiplexer #(.select(3), .width(8)) multiplexer_1 (
    .in0(register_1_q), .in1(register_2_q), .in2(register_3_q), .in3(register_4_q), .in4(register_5_q),
    .in5(register_6_q), .in6(register_7_q), .in7(register_8_q), .out(out_6), .sel(S2S1S0_2));  // open: en
  Multiplexer #(.select(3), .width(8)) multiplexer_2 (
    .in0(register_1_q), .in1(register_2_q), .in2(register_3_q), .in3(register_4_q), .in4(register_5_q),
    .in5(register_6_q), .in6(register_7_q), .in7(register_8_q), .out(out_7), .sel(S2S1S0));  // open: en
endmodule

// 3-8 decoder
module _3_to_8_decoder (
  input  A,
  input  B,
  input  C,
  output D0,
  output D1,
  output D2,
  output D3,
  output D4,
  output D5,
  output D6,
  output D7
);

  wire nand_1_out, nand_2_out, nand_3_out, nand_4_out, nand_5_out, nand_6_out, nand_7_out, nand_8_out,
       nand_9_out, nand_10_out, nand_11_out, nand_12_out, nand_13_out, nand_14_out, nand_15_out, nand_16_out,
       nand_17_out, nand_18_out, nand_19_out, nand_20_out;

  nand nand_1 (nand_1_out, A, A);
  nand nand_2 (nand_2_out, B, B);
  nand nand_3 (nand_3_out, C, C);
  nand nand_4 (nand_4_out, A, A);
  nand nand_5 (nand_5_out, B, B);
  nand nand_6 (nand_6_out, A, A);
  nand nand_7 (nand_7_out, C, C);
  nand nand_8 (nand_8_out, A, A);
  nand nand_9 (nand_9_out, B, B);
  nand nand_10 (nand_10_out, C, C);
  nand nand_11 (nand_11_out, B, B);
  nand nand_12 (nand_12_out, C, C);
  nand nand_13 (nand_13_out, A, B, C);
  nand nand_14 (nand_14_out, nand_1_out, nand_2_out, nand_3_out);
  nand nand_15 (nand_15_out, nand_4_out, nand_5_out, C);
  nand nand_16 (nand_16_out, nand_6_out, B, nand_7_out);
  nand nand_17 (nand_17_out, nand_8_out, B, C);
  nand nand_18 (nand_18_out, A, nand_9_out, nand_10_out);
  nand nand_19 (nand_19_out, A, nand_11_out, C);
  nand nand_20 (nand_20_out, A, B, nand_12_out);
  nand nand_21 (D7, nand_13_out, nand_13_out);
  nand nand_22 (D0, nand_14_out, nand_14_out);
  nand nand_23 (D1, nand_15_out, nand_15_out);
  nand nand_24 (D2, nand_16_out, nand_16_out);
  nand nand_25 (D3, nand_17_out, nand_17_out);
  nand nand_26 (D4, nand_18_out, nand_18_out);
  nand nand_27 (D5, nand_19_out, nand_19_out);
  nand nand_28 (D6, nand_20_out, nand_20_out);
endmodule

module _8x1_MUX (
  input  _0,
  input  _1,
  input  _2,
  input  _3,
  input  _4,
  input  _5,
  input  _6,
  input  _7,
  input  [2:0] S2S1S0,
  output Y
);

  wire n4x1_mux_1_y, n4x1_mux_2_y;

  _4x1_MUX u_4x1_mux_1 (.D0(_0), .D1(_1), .D2(_2), .D3(_3), .S0(S2S1S0[0]), .S1(S2S1S0[1]), .Y(n4x1_mux_1_y));
  _4x1_MUX u_4x1_mux_2 (.D0(_4), .D1(_5), .D2(_6), .D3(_7), .S0(S2S1S0[0]), .S1(S2S1S0[1]), .Y(n4x1_mux_2_y));
  _2x1_MUX u_2x1_mux_1 (.D0(n4x1_mux_1_y), .D(n4x1_mux_2_y), .S0(S2S1S0[2]), .Output(Y));
endmodule

module _8x1_Multibit_mUX (
  input  [7:0] A,
  input  [7:0] B,
  input  [7:0] C,
  input  [7:0] D,
  input  [7:0] E,
  input  [7:0] F,
  input  [7:0] G,
  input  [7:0] H,
  input  [2:0] S2S1S0,
  output [7:0] out_10
);

  _8x1_MUX u_8x1_mux_1 (
    ._0(A[0]), ._1(B[0]), ._2(C[0]), ._3(D[0]), ._4(E[0]), ._5(F[0]), ._6(G[0]), ._7(H[0]), .S2S1S0(S2S1S0),
    .Y(out_10[0]));
  _8x1_MUX u_8x1_mux_2 (
    ._0(A[1]), ._1(B[1]), ._2(C[1]), ._3(D[1]), ._4(E[1]), ._5(F[1]), ._6(G[1]), ._7(H[1]), .S2S1S0(S2S1S0),
    .Y(out_10[1]));
  _8x1_MUX u_8x1_mux_3 (
    ._0(A[2]), ._1(B[2]), ._2(C[2]), ._3(D[2]), ._4(E[2]), ._5(F[2]), ._6(G[2]), ._7(H[2]), .S2S1S0(S2S1S0),
    .Y(out_10[2]));
  _8x1_MUX u_8x1_mux_4 (
    ._0(A[3]), ._1(B[3]), ._2(C[3]), ._3(D[3]), ._4(E[3]), ._5(F[3]), ._6(G[3]), ._7(H[3]), .S2S1S0(S2S1S0),
    .Y(out_10[3]));
  _8x1_MUX u_8x1_mux_5 (
    ._0(A[4]), ._1(B[4]), ._3(D[4]), ._4(E[4]), ._5(F[4]), ._6(G[4]), ._7(H[4]), .S2S1S0(S2S1S0),
    .Y(out_10[4]));  // open: _2
  _8x1_MUX u_8x1_mux_6 (
    ._0(A[5]), ._1(B[5]), ._2(C[5]), ._3(D[5]), ._4(E[5]), ._5(F[5]), ._6(G[5]), ._7(H[5]), .S2S1S0(S2S1S0),
    .Y(out_10[5]));
  _8x1_MUX u_8x1_mux_7 (
    ._0(A[6]), ._1(B[6]), ._2(C[6]), ._3(D[6]), ._4(E[6]), ._5(F[6]), ._6(G[6]), ._7(H[6]), .S2S1S0(S2S1S0),
    .Y(out_10[6]));
  _8x1_MUX u_8x1_mux_8 (
    ._0(A[7]), ._1(B[7]), ._2(C[7]), ._3(D[7]), ._4(E[7]), ._5(F[7]), ._6(G[7]), ._7(H[7]), .S2S1S0(S2S1S0),
    .Y(out_10[7]));
endmodule

module ques_13 (
  input  A,
  input  B,
  input  constant,
  input  S1,
  input  S0,
  output out_6,
  output out_7
);

  wire n4x1_mux_1_y, not_1_out, not_2_out;

  not not_1 (not_1_out, constant);
  not not_2 (not_2_out, B);
  _4x1_MUX u_4x1_mux_1 (.D0(B), .D1(not_2_out), .D2(constant), .D3(not_1_out), .S0(S0), .S1(S1), .Y(n4x1_mux_1_y));
  Half_Adder half_adder_1 (.A(A), .B(n4x1_mux_1_y), .Sum(out_6), .Carry(out_7));
endmodule

module ques_16 (
  input  [3:0] in_1,
  input  [3:0] in_2,
  input  [3:0] in_3,
  output [3:0] out_4
);

  wire not_1_out;
  wire [3:0] n4_bit_lu_1_y3y2y1y0;

  not not_1 (not_1_out, 1'b1);
  _4_bit_LU u_4_bit_lu_1 (.A3A2A1A0(in_1), .B3B2B1B0(in_2), .S0(1'b1), .S1(not_1_out), .Y3Y2Y1Y0(n4_bit_lu_1_y3y2y1y0));
  _4_bit_LU u_4_bit_lu_2 (.A3A2A1A0(n4_bit_lu_1_y3y2y1y0), .B3B2B1B0(in_3), .S0(1'b1), .S1(1'b1), .Y3Y2Y1Y0(out_4));
endmodule

module ques_17 (
  input  in_1,
  input  in_2,
  input  in_3,
  input  in_4,
  input  in_5,
  input  in_6,
  input  in_7,
  input  in_8,
  input  complement,
  input  clr
);

  wire clock_1_out;
  wire [7:0] n2x1_bit_mux_1_out_4, not_1_out;

  Clock clock_1 (.out(clock_1_out));
  assign not_1_out = ~{in_8, in_7, in_6, in_5, in_4, in_3, in_2, in_1};  // NOT_Gate not_1, 8 bits wide
  _2x1_bit_mux u_2x1_bit_mux_1 (
    .A({in_8, in_7, in_6, in_5, in_4, in_3, in_2, in_1}), .B(not_1_out), .S0(complement),
    .out_4(n2x1_bit_mux_1_out_4));
  Register register_1 (.D(n2x1_bit_mux_1_out_4), .clk(clock_1_out), .clr(clr));  // open: en, Q
endmodule

module _2x1_bit_mux (
  input  [7:0] A,
  input  [7:0] B,
  input  S0,
  output [7:0] out_4
);

  _2x1_MUX u_2x1_mux_1 (.D0(A[0]), .D(B[0]), .S0(S0), .Output(out_4[0]));
  _2x1_MUX u_2x1_mux_2 (.D0(A[1]), .D(B[1]), .S0(S0), .Output(out_4[1]));
  _2x1_MUX u_2x1_mux_3 (.D0(A[2]), .D(B[2]), .S0(S0), .Output(out_4[2]));
  _2x1_MUX u_2x1_mux_4 (.D0(A[3]), .D(B[3]), .S0(S0), .Output(out_4[3]));
  _2x1_MUX u_2x1_mux_5 (.D0(A[4]), .D(B[4]), .S0(S0), .Output(out_4[4]));
  _2x1_MUX u_2x1_mux_6 (.D0(A[5]), .D(B[5]), .S0(S0), .Output(out_4[5]));
  _2x1_MUX u_2x1_mux_7 (.D0(A[6]), .D(B[6]), .S0(S0), .Output(out_4[6]));
  _2x1_MUX u_2x1_mux_8 (.D0(A[7]), .D(B[7]), .S0(S0), .Output(out_4[7]));
endmodule
